// Logisim project trab.circ as structural Verilog: 2 circuits, main circuit main
module main (
  input  [1:0] in_1,
  input  [7:0] in_2
);

  wire button_1_out, clk, not_1_out, not_2_out;
  wire [4:0] counter_1_q;
  wire [7:0] controlled_buffer_1_out, ram_1_data, rom_1_data;

  not not_1 (not_1_out, clk);
  Clock clock_1 (.out(clk));
  Counter #(.width(5), .max('h1f)) counter_1 (
    .Q(counter_1_q), .clk(clk), .clr(button_1_out));  // open: load, D, count, carry
  Button button_1 (.out(button_1_out));
  RAM #(.addrWidth(2), .bus("asynch")) ram_1 (.addr(in_1), .data(ram_1_data), .ld(not_1_out));  // open: sel, clr
  not not_2 (not_2_out, clk);
  assign controlled_buffer_1_out = not_2_out ? ram_1_data : 8'bz;  // Controlled_Buffer controlled_buffer_1
  assign ram_1_data = clk ? in_2 : 8'bz;  // Controlled_Buffer controlled_buffer_2
  ROM #(.addrWidth(5)) rom_1 (.addr(counter_1_q), .data(rom_1_data));  // open: sel
  assign controlled_buffer_1_out = clk ? {8{1'b0}} : 8'bz;  // Controlled_Buffer controlled_buffer_3
  LED led_1 (.in(controlled_buffer_1_out[7]));
  LED led_2 (.in(controlled_buffer_1_out[6]));
  LED led_3 (.in(controlled_buffer_1_out[5]));
  LED led_4 (.in(controlled_buffer_1_out[4]));
  LED led_5 (.in(controlled_buffer_1_out[3]));
  LED led_6 (.in(controlled_buffer_1_out[2]));
  LED led_7 (.in(controlled_buffer_1_out[1]));
  LED led_8 (.in(controlled_buffer_1_out[0]));
  instr_dec instr_dec_1 ();  // open: in_1

  // Other names for the same wires on the sheet: input[7:0] = in_2

  // Notes on the sheet:
  //   contents of rom_1 (hex, n*v repeats v):
  //   1 2 3 4 5 6 7 8
endmodule

module instr_dec (
  input  [7:0] in_1
);
endmodule
